// Digital circuit Cuarto_ModeloPin.dig as structural Verilog
module Cuarto_ModeloPin (
  input  Int1,
  input  EnRC1,
  input  Set,
  input  EnableRC,
  input  Clr,
  input  Clock,
  input  EnableEntrada_Salida,
  input  SetRE,
  input  ClrRE,
  input  DatoRS1,
  input  SetRS,
  input  ClrRS,
  input  Int2,
  input  Int3,
  input  Int4,
  input  EnRC2,
  input  DatoRS2,
  input  EnRC3,
  input  DatoRS3,
  input  EnRC4,
  input  DatoRS4,
  output Out1,
  output OutRC1,
  output OutRE1,
  output Out2,
  output Out3,
  output Out4,
  output OutRC2,
  output OutRE2,
  output OutRC3,
  output OutRE3,
  output OutRC4,
  output OutRE4
);

  wire int1_t, int2_t, int3_t, int4_t, multiplexer_1_out, multiplexer_2_out, multiplexer_3_out,
       multiplexer_4_out, multiplexer_5_out, multiplexer_6_out, multiplexer_7_out, multiplexer_8_out,
       multiplexer_9_out, multiplexer_10_out, multiplexer_11_out, multiplexer_12_out, out1_t, out2_t, out3_t,
       out4_t;

  assign Out1 = OutRC1 ? out1_t : 1'bz;  // Driver driver_1
  assign int1_t = ~OutRC1 ? Int1 : 1'bz;  // DriverInvSel driverinvsel_1
  assign Out2 = OutRC2 ? out2_t : 1'bz;  // Driver driver_2
  assign int2_t = ~OutRC2 ? Int2 : 1'bz;  // DriverInvSel driverinvsel_2
  assign Out3 = OutRC3 ? out3_t : 1'bz;  // Driver driver_3
  assign int3_t = ~OutRC3 ? Int3 : 1'bz;  // DriverInvSel driverinvsel_3
  assign Out4 = OutRC4 ? out4_t : 1'bz;  // Driver driver_4
  assign int4_t = ~OutRC4 ? Int4 : 1'bz;  // DriverInvSel driverinvsel_4
  Multiplexer multiplexer_1 (.sel(EnableRC), .in_0(OutRC1), .in_1(EnRC1), .out(multiplexer_1_out));
  Multiplexer multiplexer_2 (.sel(EnableEntrada_Salida), .in_0(OutRE1), .in_1(int1_t), .out(multiplexer_2_out));
  Multiplexer multiplexer_3 (.sel(EnableEntrada_Salida), .in_0(out1_t), .in_1(DatoRS1), .out(multiplexer_3_out));
  D_FF_AS d_ff_as_1 (.Set(Set), .D(multiplexer_1_out), .C(Clock), .Clr(Clr), .Q(OutRC1));  // open: nQ
  D_FF_AS d_ff_as_2 (.Set(SetRE), .D(multiplexer_2_out), .C(Clock), .Clr(ClrRE), .Q(OutRE1));  // open: nQ
  D_FF_AS d_ff_as_3 (.Set(SetRS), .D(multiplexer_3_out), .C(Clock), .Clr(ClrRS), .Q(out1_t));  // open: nQ
  Multiplexer multiplexer_4 (.sel(EnableRC), .in_0(OutRC2), .in_1(EnRC2), .out(multiplexer_4_out));
  Multiplexer multiplexer_5 (.sel(EnableEntrada_Salida), .in_0(OutRE2), .in_1(int2_t), .out(multiplexer_5_out));
  Multiplexer multiplexer_6 (.sel(EnableEntrada_Salida), .in_0(out2_t), .in_1(DatoRS2), .out(multiplexer_6_out));
  D_FF_AS d_ff_as_4 (.Set(Set), .D(multiplexer_4_out), .C(Clock), .Clr(Clr), .Q(OutRC2));  // open: nQ
  D_FF_AS d_ff_as_5 (.Set(SetRE), .D(multiplexer_5_out), .C(Clock), .Clr(ClrRE), .Q(OutRE2));  // open: nQ
  D_FF_AS d_ff_as_6 (.Set(SetRS), .D(multiplexer_6_out), .C(Clock), .Clr(ClrRS), .Q(out2_t));  // open: nQ
  Multiplexer multiplexer_7 (.sel(EnableRC), .in_0(OutRC3), .in_1(EnRC3), .out(multiplexer_7_out));
  Multiplexer multiplexer_8 (.sel(EnableEntrada_Salida), .in_0(OutRE3), .in_1(int3_t), .out(multiplexer_8_out));
  Multiplexer multiplexer_9 (.sel(EnableEntrada_Salida), .in_0(out3_t), .in_1(DatoRS3), .out(multiplexer_9_out));
  D_FF_AS d_ff_as_7 (.Set(Set), .D(multiplexer_7_out), .C(Clock), .Clr(Clr), .Q(OutRC3));  // open: nQ
  D_FF_AS d_ff_as_8 (.Set(SetRE), .D(multiplexer_8_out), .C(Clock), .Clr(ClrRE), .Q(OutRE3));  // open: nQ
  D_FF_AS d_ff_as_9 (.Set(SetRS), .D(multiplexer_9_out), .C(Clock), .Clr(ClrRS), .Q(out3_t));  // open: nQ
  Multiplexer multiplexer_10 (.sel(EnableRC), .in_0(OutRC4), .in_1(EnRC4), .out(multiplexer_10_out));
  Multiplexer multiplexer_11 (.sel(EnableEntrada_Salida), .in_0(OutRE4), .in_1(int4_t), .out(multiplexer_11_out));
  Multiplexer multiplexer_12 (.sel(EnableEntrada_Salida), .in_0(out4_t), .in_1(DatoRS4), .out(multiplexer_12_out));
  D_FF_AS d_ff_as_10 (.Set(Set), .D(multiplexer_10_out), .C(Clock), .Clr(Clr), .Q(OutRC4));  // open: nQ
  D_FF_AS d_ff_as_11 (.Set(SetRE), .D(multiplexer_11_out), .C(Clock), .Clr(ClrRE), .Q(OutRE4));  // open: nQ
  D_FF_AS d_ff_as_12 (.Set(SetRS), .D(multiplexer_12_out), .C(Clock), .Clr(ClrRS), .Q(out4_t));  // open: nQ

  // Other names for the same wires on the sheet: clrRC = Clr; eRC = EnableRC; eRE_RS = EnableEntrada_Salida;
  //   setRC = Set

  // Notes on the sheet:
  //   2 buffer Tri-state x4 y entrada
  //   Registros para configuración entrada/salida
  //   Registros para almacenar el estado dado que el pin fue configurado como una entrada
  //   Registros para controlar el estado del pin dado que fue configurado como una salida
endmodule
