// Digital circuit Primero_Mulltiplexor.dig as structural Verilog
module Primero_Mulltiplexor (
  input  A2,
  input  A1,
  input  A0,
  input  I0,
  input  I1,
  input  I2,
  input  I3,
  input  I4,
  input  I5,
  input  I6,
  input  I7,
  input  Enable,
  output Z
);

  wire and_1_out, and_2_out, and_3_out, and_4_out, and_5_out, and_6_out, and_7_out, and_8_out, not_1_out,
       not_2_out, not_3_out, or_1_out, or_2_out, or_3_out;

  not not_1 (not_1_out, A2);
  not not_2 (not_2_out, A1);
  not not_3 (not_3_out, A0);
  and and_1 (and_1_out, I0, not_1_out, not_2_out, not_3_out);
  and and_2 (and_2_out, I1, not_1_out, not_2_out, A0);
  and and_3 (and_3_out, I2, not_1_out, A1, not_3_out);
  and and_4 (and_4_out, I3, not_1_out, A1, A0);
  and and_5 (and_5_out, I4, A2, not_2_out, not_3_out);
  and and_6 (and_6_out, I5, A2, not_2_out, A0);
  and and_7 (and_7_out, I6, A2, A1, not_3_out);
  and and_8 (and_8_out, I7, A2, A1, A0);
  or or_1 (or_1_out, and_1_out, and_2_out, and_3_out, and_4_out);
  or or_2 (or_2_out, and_5_out, and_6_out, and_7_out, and_8_out);
  or or_3 (or_3_out, or_1_out, or_2_out);
  and and_9 (Z, or_3_out, Enable);

  // Notes on the sheet:
  //   Multiplexor 8 entradas 1 salida;
  //   entradas =  Ij (0<=j<=7)
  //   salida  = Z;
  //   Seleccionar la entrada Ij al selecionar el número binario correspondiente
  //   con los selectores Ai (0<=i<=2) junto con el Enable,
  //   donde j = (A0 = 2^0)+(A1 = 2^1)+(A2 = 2^2)
endmodule
