// Digital circuit Segundo_Demux.dig as structural Verilog
module Segundo_Demux (
  input  A1,
  input  A0,
  input  Input,
  output I0,
  output I1,
  output I2,
  output I3
);

  wire not_1_out, not_2_out;

  not not_1 (not_1_out, A1);
  not not_2 (not_2_out, A0);
  and and_1 (I0, not_1_out, not_2_out, Input);
  and and_2 (I1, not_1_out, A0, Input);
  and and_3 (I2, A1, not_2_out, Input);
  and and_4 (I3, A1, A0, Input);

  // Notes on the sheet:
  //   Demultiplexor 1 entrada 4 salidas;
  //   Seleccionar la salida Ij (0<=j<=3) con los selectores Ai (0<=i<=1)
  //   con el número binario correspondiente j = (A0 = 2^0)+(A1 = 2^1)
endmodule
