// Digital circuit Tercero_a_Flip-FlopRS.dig as structural Verilog
module Tercero_a_Flip_FlopRS (
  input  S,
  input  R,
  input  Clock,
  output Q,
  output Q_2
);

  wire nand_1_out, nand_2_out;

  nand nand_1 (nand_1_out, S, Clock);
  nand nand_2 (nand_2_out, Clock, R);
  nand nand_3 (Q, nand_1_out, Q_2);
  nand nand_4 (Q_2, Q, nand_2_out);

  // Notes on the sheet:
  //   El flip-flop tiene dos entradas R (reset) y S (set).
  //   El flip-flop RS síncrono opera en conjunción con un reloj.
  //   Cuando un pulso de reloj llega a la entrada CLK (con 0 en las entradas R y S), las salidas no cambian,
  //   este modo también puede llamarse de inhabilitación.
  //   La salida Q se borrará cuando se active la entrada R y un pulso de reloj active la entrada clock. 
  //   Si R=1 y S=0, el FF no se pone a 0 inmediatamente, esperará hasta que el pulso del reloj pase del nivel 0 a 1.
  //   Un 1 en la entrada S (con R=0 y un pulso de reloj en 1), pone la salida Q a 1. 
  //   La combinación "prohibida" es donde todas las entradas estén en 1, no se utiliza porque activa ambas salidas.
endmodule
