// Digital circuit Tercero_b_Flip-FlopJK.dig as structural Verilog
module Tercero_b_Flip_FlopJK (
  input  J,
  input  K,
  input  Clock,
  input  J_ms,
  input  K_ms,
  input  Clock_2,
  output Q,
  output Q_2,
  output Q_ms,
  output Q__ms
);

  wire clock_t, nand_1_out, nand_2_out, nand_3_out, nand_4_out, nand_5_out, nand_6_out, nand_9_out,
       nand_10_out;

  nand nand_1 (nand_1_out, Q__ms, J_ms, Clock_2);
  nand nand_2 (nand_2_out, Clock_2, K_ms, Q_ms);
  not not_1 (clock_t, Clock_2);
  nand nand_3 (nand_3_out, Q_2, J, Clock);
  nand nand_4 (nand_4_out, Clock, K, Q);
  nand nand_5 (nand_5_out, nand_1_out, nand_6_out);
  nand nand_6 (nand_6_out, nand_5_out, nand_2_out);
  nand nand_7 (Q, nand_3_out, Q_2);
  nand nand_8 (Q_2, Q, nand_4_out);
  nand nand_9 (nand_9_out, nand_5_out, clock_t);
  nand nand_10 (nand_10_out, clock_t, nand_6_out);
  nand nand_11 (Q_ms, nand_9_out, Q__ms);
  nand nand_12 (Q__ms, Q_ms, nand_10_out);

  // Notes on the sheet:
  //   Si J y K son diferentes, la salida Q toma el valor de J durante la subida del siguiente pulso de sincronismo.
  //   El encendido del clock habilita la permutación de la salida Q.
  //   Como esta versión de 4-NAND del flip-flop J-K está sometida al problema de la "carrera", 
  //   se desarrollo el Flip Flop J-K Master-Slave para proporcionar un circuito más estable con la misma función,
  //   donde la transmisión del valor J a la salida se retrasa medio ciclo de clock y no se retroalimenta
  //   inmediatamente a la entrada.
  //   Las salidas se retroalimentan a las puertas NAND habilitadas,
  //   esto es lo que le da la acción de conmutación cuando J=K=1.
  //   Flip-Flop JK Master-Slave
  //   Flip-Flop JK
  //   Master
  //   Slave
endmodule
